# Fritzing sketch raspi and 2 leds (saved by Fritzing 0.9.2b)
breadboards: 1

parts:
  LED1 = LED - 3mm [color="Red (633nm)" package="3 mm [THT]"]
  R2 = Resistor [tolerance=±5% resistance=220 package=THT]
  R3 = Resistor [tolerance=±5% resistance=220 package=THT]
  LED2 = LED - 3mm [color="Red (633nm)" package="3 mm [THT]"]
  Raspberry_Pi1 = Raspberry Pi 2

nets:
  N1: LED1.cathode, LED2.cathode, Raspberry_Pi1.GND
  N2: LED1.anode, R2.Pin_0
  N3: R2.Pin_1, Raspberry_Pi1.GPIO14
  N4: R3.Pin_0, LED2.anode
  N5: R3.Pin_1, Raspberry_Pi1.GPIO15
