# Fritzing sketch raspi and 2 switches (saved by Fritzing 0.9.2b)
breadboards: 1

parts:
  S1 = Pushbutton [package="[THT]"]
  S2 = Pushbutton [package="[THT]"]
  Raspberry_Pi1 = Raspberry Pi 2

nets:
  N1: S1.Pin_1, S1.Pin_2, S2.Pin_1, S2.Pin_2, Raspberry_Pi1.GND
  N2: S1.Pin_3, S1.Pin_4, Raspberry_Pi1.GPIO23
  N3: S2.Pin_3, S2.Pin_4, Raspberry_Pi1.GPIO24
